// Digital circuit EX-MEM.dig as structural Verilog
module EX_MEM (
  input  clk,
  input  rst,
  input  cmp_result,
  input  [31:0] alu_result,
  input  [3:0] memory_op,
  input  [31:0] r2,
  input  rf_write,
  input  [1:0] rf_in_sel,
  input  [4:0] rd,
  input  [31:0] pc,
  input  pc_load,
  input  pc_in_sel,
  output cmp_result_out,
  output [31:0] alu_result_out,
  output [3:0] memory_op_out,
  output [31:0] r2_out,
  output [4:0] rd_out,
  output rf_write_out,
  output [1:0] rf_in_sel_out,
  output [31:0] pc_out,
  output pc_load_out,
  output pc_in_sel_out
);

  EX_MEM #(.applicationType("IVERILOG")) u_EX_MEM (
    .clk(clk), .rst(rst), .cmp_result(cmp_result), .alu_result(alu_result), .memory_op(memory_op), .r2(r2),
    .rd(rd), .rf_write(rf_write), .rf_in_sel(rf_in_sel), .pc(pc), .pc_load(pc_load), .pc_in_sel(pc_in_sel),
    .cmp_result_out(cmp_result_out), .alu_result_out(alu_result_out), .r2_out(r2_out),
    .memory_op_out(memory_op_out), .rd_out(rd_out), .rf_write_out(rf_write_out),
    .rf_in_sel_out(rf_in_sel_out), .pc_out(pc_out), .pc_load_out(pc_load_out), .pc_in_sel_out(pc_in_sel_out));
endmodule

/* Code of EX_MEM:
`define MEM_NOP 4'b1111

module EX_MEM(clk,rst,cmp_result,alu_result,memory_op,r2,rd,rf_write,
	rf_in_sel,pc,pc_load,pc_in_sel,
	cmp_result_out,alu_result_out,memory_op_out,r2_out,rd_out,rf_write_out,
	rf_in_sel_out,pc_out,pc_load_out,pc_in_sel_out);
	
	input clk, rst, cmp_result;
	input [31:0] alu_result;
	input [3:0] memory_op;
	input [31:0] r2;
	input [4:0] rd;
	input rf_write;
	input [1:0] rf_in_sel;
	input [31:0] pc;
	input pc_load, pc_in_sel;

	output cmp_result_out;
	output [31:0] alu_result_out;
	output [31:0] r2_out;
	output [3:0] memory_op_out;
	output [4:0] rd_out; 
	output rf_write_out;
	output [1:0] rf_in_sel_out;
	output [31:0] pc_out;
	output pc_load_out, pc_in_sel_out;
	
	// cmp_result_out 初始值设置为1
	reg cmp_result_out = 1;
	reg [31:0] alu_result_out;
	reg [3:0] memory_op_out = `MEM_NOP;
	reg [31:0] r2_out;
	reg [4:0] rd_out;  
	reg rf_write_out;
	reg [1:0] rf_in_sel_out;
	reg [31:0] pc_out;
	// pc_load_out 初始值设置为1
	reg pc_load_out = 1, pc_in_sel_out;

	always @(posedge clk)
	begin
		if(rst)
		begin
			cmp_result_out = 0;
			alu_result_out = 0;
			memory_op_out = `MEM_NOP;
			r2_out = 0;
			rd_out = 0; 
			rf_write_out = 0;
			rf_in_sel_out = 0;
			pc_out = 0;
			pc_load_out = 0;
			pc_in_sel_out = 0;
		end
		else
		begin
			cmp_result_out = cmp_result;
			alu_result_out = alu_result;
			memory_op_out = memory_op;
			r2_out = r2;
			rd_out = rd; 
			rf_write_out = rf_write;
			rf_in_sel_out = rf_in_sel;
			pc_out = pc;
			pc_load_out = pc_load;
			pc_in_sel_out = pc_in_sel;
		end
	end

endmodule
*/
