// Digital circuit ID-EX.dig as structural Verilog
module ID_EX (
  input  clk,
  input  rst,
  input  [31:0] pc,
  input  [31:0] r1,
  input  [31:0] r2,
  input  [31:0] imm,
  input  [3:0] memory_op,
  input  [3:0] alu_op,
  input  [2:0] cmp_op,
  input  r1_pc_sel,
  input  r2_imm_sel,
  input  pc_load,
  input  pc_in_sel,
  input  rf_write,
  input  [1:0] rf_in_sel,
  input  [4:0] rd,
  input  [4:0] rs1,
  input  [4:0] rs2,
  output [1:0] rf_in_sel_out,
  output pc_in_sel_out,
  output [3:0] memory_op_out,
  output [3:0] alu_op_out,
  output r2_imm_sel_out,
  output pc_load_out,
  output rf_write_out,
  output r1_pc_sel_out,
  output [2:0] cmp_op_out,
  output [31:0] imm_out,
  output [31:0] r2_out,
  output [31:0] r1_out,
  output [31:0] pc_out,
  output [4:0] rd_out,
  output [4:0] rs1_out,
  output [4:0] rs2_out
);

  ID_EX #(.applicationType("IVERILOG")) u_ID_EX (
    .clk(clk), .rst(rst), .pc(pc), .r1(r1), .r2(r2), .rd(rd), .imm(imm), .memory_op(memory_op),
    .alu_op(alu_op), .cmp_op(cmp_op), .r1_pc_sel(r1_pc_sel), .r2_imm_sel(r2_imm_sel), .pc_load(pc_load),
    .pc_in_sel(pc_in_sel), .rf_write(rf_write), .rf_in_sel(rf_in_sel), .rs1(rs1), .rs2(rs2), .pc_out(pc_out),
    .r1_out(r1_out), .r2_out(r2_out), .rd_out(rd_out), .imm_out(imm_out), .memory_op_out(memory_op_out),
    .alu_op_out(alu_op_out), .cmp_op_out(cmp_op_out), .r1_pc_sel_out(r1_pc_sel_out),
    .r2_imm_sel_out(r2_imm_sel_out), .pc_load_out(pc_load_out), .pc_in_sel_out(pc_in_sel_out),
    .rf_write_out(rf_write_out), .rf_in_sel_out(rf_in_sel_out), .rs1_out(rs1_out), .rs2_out(rs2_out));

  // Notes on the sheet:
  //   rf_in_sel_out: rf-din输入选择信号
  //   pc_in_sel_out: pc输入选择信号
  //   memory_op_out: 存储器控制信号
  //   alu_op_out: alu控制信号
  //   r2_imm_sel_out: r2, imm 选择控制信号
  //   pc_load_out: pc是否要加载下一条指令的控制信号
  //   rf_write_out: rf 写 控制信号
endmodule

/* Code of ID_EX:
`define MEM_NOP 4'b1111
`define CMP_NOP 3'b010

module ID_EX(clk,rst,pc,r1,r2,rd,imm,memory_op,alu_op,cmp_op,r1_pc_sel, 
	r2_imm_sel,pc_load,pc_in_sel,rf_write,rf_in_sel, rs1, rs2, 
	pc_out,r1_out,r2_out,rd_out,imm_out,memory_op_out,alu_op_out,cmp_op_out,
	r1_pc_sel_out,r2_imm_sel_out,pc_load_out,pc_in_sel_out,rf_write_out,
	rf_in_sel_out, rs1_out, rs2_out);

	input clk, rst;
	input [31:0] pc, r1, r2;
	input [4:0] rd;
	input [31:0] imm;
	input [3:0] memory_op, alu_op;
	input [2:0] cmp_op;
	input r1_pc_sel, r2_imm_sel, pc_load, pc_in_sel, rf_write;
	input [1:0] rf_in_sel;
	input [4:0] rs1, rs2;

	output [31:0] pc_out, r1_out, r2_out;
	output [4:0] rd_out;
	output [31:0] imm_out;
	output [3:0] memory_op_out, alu_op_out;
	output [2:0] cmp_op_out;
	output r1_pc_sel_out, r2_imm_sel_out, pc_load_out, pc_in_sel_out, rf_write_out;
	output [1:0] rf_in_sel_out;
	output [4:0] rs1_out, rs2_out;
	
	reg [31:0] pc_out, r1_out, r2_out;
	reg [4:0] rd_out;
	reg [31:0] imm_out;
	reg [3:0] memory_op_out = `MEM_NOP, alu_op_out;
	reg [2:0] cmp_op_out = `CMP_NOP;
	// pc_load_out 初始值设为1，使得流水线刚启动时能顺利运行下去
	reg r1_pc_sel_out, r2_imm_sel_out, pc_load_out = 1, pc_in_sel_out, rf_write_out;
	reg [1:0] rf_in_sel_out;
	reg [4:0] rs1_out, rs2_out;
	
	always @(posedge clk)
	begin
		if (rst)
		begin
			pc_out = 0;
			r1_out = 0;
			r2_out = 0;
			rd_out = 0;
			imm_out = 0;
			memory_op_out = `MEM_NOP;
			alu_op_out = 0;
			cmp_op_out = `CMP_NOP;
			r1_pc_sel_out = 0;
			r2_imm_sel_out = 0;
			pc_load_out = 0;
			pc_in_sel_out = 0;
			rf_write_out = 0;
			rf_in_sel_out = 0;
			rs1_out = 0;
			rs2_out = 0;
		end
		else
		begin
			pc_out = pc;
			r1_out = r1;
			r2_out = r2;
			rd_out = rd;
			imm_out = imm;
			memory_op_out = memory_op;
			alu_op_out = alu_op;
			cmp_op_out = cmp_op;
			r1_pc_sel_out = r1_pc_sel;
			r2_imm_sel_out = r2_imm_sel;
			pc_load_out = pc_load;
			pc_in_sel_out = pc_in_sel;
			rf_write_out = rf_write;
			rf_in_sel_out = rf_in_sel;
			rs1_out = rs1;
			rs2_out = rs2;
		end
	end
endmodule
*/
