// Digital circuit IF-ID.dig as structural Verilog
module IF_ID (
  input  [31:0] pc_in,
  input  [31:0] inst_in,
  input  clk,
  input  rst,
  input  write,
  output [31:0] pc_out,
  output [31:0] inst_out
);

  IF_ID #(.applicationType("IVERILOG")) u_IF_ID (
    .clk(clk), .rst(rst), .write(write), .pc_in(pc_in), .inst_in(inst_in), .pc_out(pc_out),
    .inst_out(inst_out));
endmodule

/* Code of IF_ID:
module IF_ID(clk, rst, write, pc_in, inst_in, pc_out, inst_out);
	input clk, rst, write;
	input [31:0] pc_in, inst_in;
	output [31:0] pc_out, inst_out;
	
	reg [31:0] pc_out, inst_out;
	
	always @(posedge clk)
	begin
		if (rst)
		begin
			pc_out = 0;
			// rst时，将指令置为'0号寄存器加0放到0号寄存器'这样的无效指令
			inst_out = 'h00000013;
		end
		else if (write)
		begin
			pc_out = pc_in;
			inst_out = inst_in;
		end
	end

endmodule
*/
