// Digital circuit MEM-WB.dig as structural Verilog
module MEM_WB (
  input  clk,
  input  rst,
  input  rf_write,
  input  [1:0] rf_in_sel,
  input  [31:0] dout,
  input  [31:0] pc,
  input  [31:0] alu_result,
  input  [4:0] rd,
  output [4:0] rd_out,
  output rf_write_out,
  output [1:0] rf_in_sel_out,
  output [31:0] alu_result_out,
  output [31:0] dout_out,
  output [31:0] pc_out
);

  MEM_WB #(.applicationType("IVERILOG")) u_MEM_WB (
    .clk(clk), .rst(rst), .rd(rd), .rf_write(rf_write), .rf_in_sel(rf_in_sel), .alu_result(alu_result),
    .dout(dout), .pc(pc), .rd_out(rd_out), .rf_write_out(rf_write_out), .rf_in_sel_out(rf_in_sel_out),
    .alu_result_out(alu_result_out), .dout_out(dout_out), .pc_out(pc_out));
endmodule

/* Code of MEM_WB:
module MEM_WB(clk,rst,rd,rf_write,rf_in_sel,alu_result,dout,pc,
	rd_out,rf_write_out,rf_in_sel_out,alu_result_out,dout_out,pc_out);

	input clk, rst;
	input [4:0] rd;
	input rf_write;
	input [1:0] rf_in_sel;
	input [31:0] alu_result, dout, pc;
	
	output [4:0] rd_out;
	output rf_write_out;
	output [1:0] rf_in_sel_out;
	output [31:0] alu_result_out, dout_out, pc_out;

	reg [4:0] rd_out;
	reg rf_write_out;
	reg [1:0] rf_in_sel_out;
	reg [31:0] alu_result_out, dout_out, pc_out;

	always @(posedge clk)
	begin
		if (rst)
		begin
			rd_out = 0;
			rf_write_out = 0;
			rf_in_sel_out = 0;
			alu_result_out = 0;
			dout_out = 0;
			pc_out = 0;
		end
		else
		begin
			rd_out = rd;
			rf_write_out = rf_write;
			rf_in_sel_out = rf_in_sel;
			alu_result_out = alu_result;
			dout_out = dout;
			pc_out = pc;
		end
	end
endmodule
*/
