// Digital circuit alu-discard.dig as structural Verilog
module alu_discard (
  input  [3:0] op,
  input  [31:0] in1,
  input  [31:0] in2,
  output [31:0] out
);

  alu #(.applicationType("IVERILOG")) u_alu (.op(op), .in1(in1), .in2(in2), .out(out));

  // Notes on the sheet:
  //   op: 操作指令
  //   in1: 输入1
  //   in2: 输入2
  //   out: 计算结果
endmodule

/* Code of alu:
// addi, xori, slli，等立即数操作，由控制器来控制输入ALU的是寄存器数据还是立即数，
// ALU只负责计算in1和in2

// ALU_arithmetic_opcode = inst[30|14:12]
// ALU_logic_opcode = 1|inst[14:12]（除beq和bge）（最高位始终为1）
// 由于beq与sub编码冲突，beq设为1010
// 由于bge与sra编码冲突，bge设为1011
/*
`define ALU_ADD 0
`define ALU_SUB 8
`define ALU_SLL 1
`define ALU_SLT 2
`define ALU_SLTU 3
`define ALU_XOR 4
`define ALU_SRL 5
`define ALU_SRA 13
`define ALU_OR 6
`define ALU_AND 7
* /
// 算术运算
`define ALU_ADD 4'b0000
`define ALU_SUB 4'b1000
`define ALU_SLL 4'b0001
`define ALU_SLT 4'b0010
`define ALU_SLTU 4'b0011
`define ALU_XOR 4'b0100
`define ALU_SRL 4'b0101
`define ALU_SRA 4'b1101
`define ALU_OR 4'b0110
`define ALU_AND 4'b0111
// 逻辑运算
`define ALU_BEQ 4'b1010
`define ALU_BNE 4'b1001
`define ALU_BLT 4'b1100
`define ALU_BGE 4'b1011
`define ALU_BLTU 4'b1110
`define ALU_BGEU 4'b1111

module alu(op, in1, in2, out);
	input [3:0] op;
	input [31:0] in1, in2;
	output [31:0] out;

	reg [31:0] out;
	
	// 当op或in1或in2 发生变化时，执行下面代码
	always @(op or in1 or in2)
	begin
		case(op)
			// 算术运算
			`ALU_ADD: out = in1 + in2;
			`ALU_SUB: out = in1 - in2;
			// 逻辑左移
			// 移位操作数是无符号数，且只取低5位作为有效数
			`ALU_SLL: out = in1 << in2[4:0];
			`ALU_SLT: 
				if($signed(in1) < $signed(in2)) 
					out = 1; 
				else
					out = 0;
			`ALU_SLTU:
				if($unsigned(in1) < $unsigned(in2)) 
					out = 1; 
				else
					out = 0;
			`ALU_XOR: out = in1 ^ in2;
			// 逻辑右移
			`ALU_SRL: out = in1 >> in2[4:0];
			// 算术右移
			// 这里取低5位作为有效数，
			// 也有效的避免了srai操作中imm中第十位为1造成的影响
			`ALU_SRA: out = $signed(in1) >>> in2[4:0];
			`ALU_OR: out = in1 | in2;
			`ALU_AND: out = in1 & in2;
			
			// 逻辑运算
			`ALU_BEQ:
				if($signed(in1) == $signed(in2)) 
					out = 1; 
				else
					out = 0;
			`ALU_BNE:
				if($signed(in1) != $signed(in2)) 
					out = 1; 
				else
					out = 0;
			`ALU_BLT:
				if($signed(in1) < $signed(in2)) 
					out = 1; 
				else
					out = 0;
			`ALU_BGE:
				if($signed(in1) >= $signed(in2)) 
					out = 1; 
				else
					out = 0;
			`ALU_BLTU:
				if($unsigned(in1) < $unsigned(in2)) 
					out = 1; 
				else
					out = 0;
			`ALU_BGEU:
				if($unsigned(in1) >= $unsigned(in2)) 
					out = 1; 
				else
					out = 0;
			default: out = 0;
		endcase
	end
endmodule
*/
