// Digital circuit cmp.dig as structural Verilog
// 比较单元
// 输出0或1
module cmp (
  input  [31:0] in1,
  input  [31:0] in2,
  input  [2:0] op,
  output out
);

  cmp #(.applicationType("IVERILOG")) u_cmp (.op(op), .in1(in1), .in2(in2), .out(out));
endmodule

/* Code of cmp:
`define CMP_BEQ 3'b000
`define CMP_BNE 3'b001
`define CMP_BLT 3'b100
`define CMP_BGE 3'b101
`define CMP_BLTU 3'b110
`define CMP_BGEU 3'b111
`define CMP_DONOTHING 3'b010

module cmp(op, in1, in2, out);
	input [2:0] op;
	input [31:0] in1, in2;
	output out;

	reg out = 1;

	always @(op, in1, in2)
	begin
		case(op)
			// 逻辑运算
			`CMP_BEQ:
				if($signed(in1) == $signed(in2)) 
					out = 1; 
				else
					out = 0;
			`CMP_BNE:
				if($signed(in1) != $signed(in2)) 
					out = 1; 
				else
					out = 0;
			`CMP_BLT:
				if($signed(in1) < $signed(in2)) 
					out = 1; 
				else
					out = 0;
			`CMP_BGE:
				if($signed(in1) >= $signed(in2)) 
					out = 1; 
				else
					out = 0;
			`CMP_BLTU:
				if($unsigned(in1) < $unsigned(in2)) 
					out = 1; 
				else
					out = 0;
			`CMP_BGEU:
				if($unsigned(in1) >= $unsigned(in2)) 
					out = 1; 
				else
					out = 1;
			default: out = 0;
		endcase
	end
endmodule
*/
