// Digital circuit code.dig as structural Verilog
// 根据指令前8位的地址，取出完整32位指令
module code (
  input  [31:0] pc,
  output [31:0] inst
);

  code #(.applicationType("IVERILOG")) u_code (.pc(pc), .inst(inst));

  // Notes on the sheet:
  //   pc: 指令地址
  //   inst: 32位的指令
endmodule

/* Code of code:
module code(pc, inst);
	input [31:0] pc;
	output [31:0] inst;
	
	reg [31:0] inst;
	// 提供2^16字节 地址空间
	reg [7:0] r[0:65536];
	
	always @(pc)
	begin
		// 组装指令
		inst[31: 24] = r[pc];
		inst[23: 16] = r[pc+1];
		inst[15: 8] = r[pc+2];
		inst[7: 0] = r[pc+3];
	end

	initial
	begin
r[0] = 8'b00000000;
r[1] = 8'b00010000;
r[2] = 8'b00000000;
r[3] = 8'b10010011;

r[4] = 8'b00000000;
r[5] = 8'b00100000;
r[6] = 8'b00000001;
r[7] = 8'b00010011;

r[8] = 8'b00000000;
r[9] = 8'b00100000;
r[10] = 8'b10000001;
r[11] = 8'b10110011;

r[12] = 8'b00000000;
r[13] = 8'b00110000;
r[14] = 8'b00100000;
r[15] = 8'b00100011;

	end
endmodule
*/
