// Digital circuit code_new.dig as structural Verilog
module code_new (
  input  [31:0] address,
  output [31:0] inst
);

  ROM #(.AddrBits(20), .Bits(32)) rom_1 (.A(address[21:2]), .sel(1'b1), .D(inst));
endmodule
