// Digital circuit forwarding_unit.dig as structural Verilog
module forwarding_unit (
  input  [4:0] rs1_IDEX,
  input  [4:0] rs2_IDEX,
  input  write_EXMEM,
  input  [4:0] rd_EXMEM,
  input  write_MEMWB,
  input  [4:0] rd_MEMWB,
  input  [4:0] rs2_ID,
  input  [4:0] rs1_ID,
  input  write_IDEX,
  input  [4:0] rd_IDEX,
  output [1:0] forward_alu1,
  output [1:0] forward_alu2,
  output [1:0] forward_cmp1,
  output [1:0] forward_cmp2
);

  forwarding_unit #(.applicationType("IVERILOG")) u_forwarding_unit (
    .rs1_ID(rs1_ID), .rs2_ID(rs2_ID), .rs1_IDEX(rs1_IDEX), .rs2_IDEX(rs2_IDEX), .rd_IDEX(rd_IDEX),
    .write_IDEX(write_IDEX), .rd_EXMEM(rd_EXMEM), .write_EXMEM(write_EXMEM), .rd_MEMWB(rd_MEMWB),
    .write_MEMWB(write_MEMWB), .forward_alu1(forward_alu1), .forward_alu2(forward_alu2),
    .forward_cmp1(forward_cmp1), .forward_cmp2(forward_cmp2));
endmodule

/* Code of forwarding_unit:
module forwarding_unit(rs1_ID, rs2_ID, rs1_IDEX, rs2_IDEX, 
	rd_IDEX, write_IDEX, rd_EXMEM, write_EXMEM, rd_MEMWB, write_MEMWB,
	forward_alu1, forward_alu2, forward_cmp1, forward_cmp2);
	
	input [4:0] rs1_ID, rs2_ID, rs1_IDEX, rs2_IDEX;
	input [4:0] rd_IDEX; 
	input write_IDEX;
	input [4:0] rd_EXMEM; 
	input write_EXMEM;
	input [4:0] rd_MEMWB;
	input write_MEMWB;
	output [1:0] forward_alu1, forward_alu2, forward_cmp1, forward_cmp2;
	
	assign forward_alu1 = (write_EXMEM && rd_EXMEM != 0 && rd_EXMEM == rs1_IDEX) ? 10 :
			   (write_MEMWB && rd_MEMWB != 0 && rd_MEMWB == rs1_IDEX) ? 01 : 00;

	assign forward_alu2 = (write_EXMEM && rd_EXMEM != 0 && rd_EXMEM == rs2_IDEX) ? 10 :
			   (write_MEMWB && rd_MEMWB != 0 && rd_MEMWB == rs2_IDEX) ? 01 : 00;
	
	assign forward_cmp1 = (write_IDEX && rd_IDEX != 0 && rd_IDEX == rs1_ID) ? 10 :
				(write_EXMEM && rd_EXMEM != 0 && rd_EXMEM == rs1_ID) ? 01 : 00;
	
	assign forward_cmp2 = (write_IDEX && rd_IDEX != 0 && rd_IDEX == rs2_ID) ? 10 :
				(write_EXMEM && rd_EXMEM != 0 && rd_EXMEM == rs2_ID) ? 01 : 00;
endmodule
*/
