// Digital circuit hazard_detection_unit.dig as structural Verilog
module hazard_detection_unit (
  input  [4:0] rs1_IFID,
  input  [4:0] rs2_IFID,
  input  [4:0] rd_IDEX,
  input  [3:0] memop_IDEX,
  input  jump,
  output load,
  output write_IFID,
  output zero_IDEX,
  output zero_IFID
);

  hazard_detection #(.applicationType("IVERILOG")) u_hazard_detection (
    .rs1_IFID(rs1_IFID), .rs2_IFID(rs2_IFID), .rd_IDEX(rd_IDEX), .memop_IDEX(memop_IDEX), .jump(jump),
    .load(load), .write_IFID(write_IFID), .zero_IFID(zero_IFID), .zero_IDEX(zero_IDEX));
endmodule

/* Code of hazard_detection:
// memory_op
// memory_op = inst[6|14:12] = opcode[6] + funct[2:0]
`define LB 4'b0000
`define LH 4'b0001
`define LW 4'b0010
`define LBU 4'b0100
`define LHU 4'b0101
`define SB 4'b1000
`define SH 4'b1001
`define SW 4'b1010
`define MEM_NOP 4'b1111

module hazard_detection(rs1_IFID, rs2_IFID, rd_IDEX, memop_IDEX, jump,
	load, write_IFID, zero_IFID, zero_IDEX);
	
	input [4:0] rs1_IFID, rs2_IFID, rd_IDEX;
	input [3:0] memop_IDEX;
	input jump;

	output load, write_IFID, zero_IFID, zero_IDEX;
	
	assign load = (memop_IDEX[3] == 0 && rd_IDEX != 0 && (rd_IDEX == rs1_IFID || rd_IDEX == rs2_IFID)) ? 0 : 1;
	assign write_IFID = (memop_IDEX[3] == 0 && rd_IDEX != 0 && (rd_IDEX == rs1_IFID || rd_IDEX == rs2_IFID)) ? 0 : 1;
	assign zero_IDEX = (memop_IDEX[3] == 0 && rd_IDEX != 0 && (rd_IDEX == rs1_IFID || rd_IDEX == rs2_IFID)) ? 1 : 0;
	// 当branch指令结果为跳转，且未发生load-use hazard时，另zero_IFID为0
	assign zero_IFID = (!(memop_IDEX[3] == 0 && rd_IDEX != 0 && (rd_IDEX == rs1_IFID || rd_IDEX == rs2_IFID)) && jump == 1) ? 1 : 0;
endmodule
*/
