// Digital circuit lu.dig as structural Verilog
// 逻辑运算单元
// 输出0或1
module lu (
  input  [31:0] in1,
  input  [31:0] in2,
  input  [2:0] op,
  output out
);

  lu #(.applicationType("IVERILOG")) u_lu (.op(op), .in1(in1), .in2(in2), .out(out));
endmodule

/* Code of lu:
`define LU_BEQ 3'b000
`define LU_BNE 3'b001
`define LU_BLT 3'b100
`define LU_BGE 3'b101
`define LU_BLTU 3'b110
`define LU_BGEU 3'b111
`define LU_DONOTHING 3b'010

module lu(op, in1, in2, out);
	input [2:0] op;
	input [31:0] in1, in2;
	output out;

	reg out = 1;

	always @(op, in1, in2)
	begin
		case(op)
			// 逻辑运算
			`LU_BEQ:
				if($signed(in1) == $signed(in2)) 
					out = 1; 
				else
					out = 0;
			`LU_BNE:
				if($signed(in1) != $signed(in2)) 
					out = 1; 
				else
					out = 0;
			`LU_BLT:
				if($signed(in1) < $signed(in2)) 
					out = 1; 
				else
					out = 0;
			`LU_BGE:
				if($signed(in1) >= $signed(in2)) 
					out = 1; 
				else
					out = 0;
			`LU_BLTU:
				if($unsigned(in1) < $unsigned(in2)) 
					out = 1; 
				else
					out = 0;
			`LU_BGEU:
				if($unsigned(in1) >= $unsigned(in2)) 
					out = 1; 
				else
					out = 0;
			default: out = 1;
		endcase
	end
endmodule
*/
