// Digital circuit main.dig as structural Verilog
module main (
  input  rst,
  input  clk
);

  wire and_1_out, and_2_out, cmp_1_out, controller_1_pc_in_sel, controller_1_r1_pc_sel,
       controller_1_r2_imm_sel, controller_1_rf_write, ex_mem_1_p14, hazard_detection_unit_1_load,
       hazard_detection_unit_1_write_ifid, hazard_detection_unit_1_zero_idex,
       hazard_detection_unit_1_zero_ifid, id_ex_1_p23, id_ex_1_p24, id_ex_1_p25, id_ex_1_p26,
       mem_wb_1_rf_write_out, not_1_out, or_1_out, or_2_out;
  wire [1:0] controller_1_rf_in_sel, ex_mem_1_p15, forwarding_unit_1_forward_alu1,
       forwarding_unit_1_forward_alu2, forwarding_unit_1_forward_cmp1, forwarding_unit_1_forward_cmp2,
       mem_wb_1_rf_in_sel_out;
  wire [2:0] controller_1_cmp_op;
  wire [3:0] controller_1_alu_op, controller_1_memory_op, ex_mem_1_p12, id_ex_1_p21, id_ex_1_p22;
  wire [4:0] decode_1_rd, decode_1_rs1, decode_1_rs2, ex_mem_1_p13, id_ex_1_p19, id_ex_1_p27, id_ex_1_p28,
       mem_wb_1_rd_out;
  wire [6:0] decode_1_opcode;
  wire [9:0] decode_1_funct;
  wire [31:0] add_1_s, add_2_s, alu_1_out, code_1_inst, decode_1_imm, ex_mem_1_p10, ex_mem_1_p11,
       ex_mem_1_p16, id_ex_1_p16, id_ex_1_p17, id_ex_1_p18, id_ex_1_p20, if_id_1_inst_out, if_id_1_pc_out,
       mem_wb_1_alu_result_out, mem_wb_1_dout_out, mem_wb_1_pc_out, memory_1_dout, multiplexer_1_out,
       multiplexer_2_out, multiplexer_3_out, multiplexer_4_out, multiplexer_5_out, multiplexer_6_out,
       multiplexer_7_out, multiplexer_8_out, multiplexer_9_out, pc_1_dout, pc_4_1_pc_out, regfile_1_r1,
       regfile_1_r2;

  Multiplexer #(.Bits(32)) multiplexer_1 (
    .sel(and_1_out), .in_0(pc_4_1_pc_out), .in_1(add_1_s), .out(multiplexer_1_out));
  pc_4 pc_4_1 (.pc_out(pc_4_1_pc_out), .pc(pc_1_dout));
  pc pc_1 (.clk(clk), .rst(rst), .load(hazard_detection_unit_1_load), .din(multiplexer_1_out), .dout(pc_1_dout));
  code code_1 (.pc(pc_1_dout), .inst(code_1_inst));
  or or_1 (or_1_out, hazard_detection_unit_1_zero_ifid, rst);
  IF_ID if_id_1 (
    .clk(clk), .rst(or_1_out), .write(hazard_detection_unit_1_write_ifid), .pc_in(pc_1_dout),
    .inst_in(code_1_inst), .pc_out(if_id_1_pc_out), .inst_out(if_id_1_inst_out));
  decode decode_1 (
    .inst(if_id_1_inst_out), .opcode(decode_1_opcode), .funct(decode_1_funct), .rs1(decode_1_rs1),
    .rs2(decode_1_rs2), .rd(decode_1_rd), .imm(decode_1_imm));
  hazard_detection_unit hazard_detection_unit_1 (
    .rs1_IFID(decode_1_rs1), .rs2_IFID(decode_1_rs2), .rd_IDEX(id_ex_1_p19), .memop_IDEX(id_ex_1_p21),
    .jump(and_1_out), .load(hazard_detection_unit_1_load), .write_IFID(hazard_detection_unit_1_write_ifid),
    .zero_IFID(hazard_detection_unit_1_zero_ifid), .zero_IDEX(hazard_detection_unit_1_zero_idex));
  regfile regfile_1 (
    .clk(clk), .rst(rst), .rs1(decode_1_rs1), .rs2(decode_1_rs2), .rd(mem_wb_1_rd_out),
    .write(mem_wb_1_rf_write_out), .din(multiplexer_9_out), .r1(regfile_1_r1), .r2(regfile_1_r2));
  controller controller_1 (
    .memory_op(controller_1_memory_op), .alu_op(controller_1_alu_op), .cmp_op(controller_1_cmp_op),
    .r1_pc_sel(controller_1_r1_pc_sel), .r2_imm_sel(controller_1_r2_imm_sel),
    .pc_in_sel(controller_1_pc_in_sel), .rf_write(controller_1_rf_write), .rf_in_sel(controller_1_rf_in_sel),
    .clk(clk), .rst(rst), .opcode(decode_1_opcode), .funct(decode_1_funct));
  Multiplexer #(.Selector_Bits(2), .Bits(32)) multiplexer_2 (
    .sel(forwarding_unit_1_forward_cmp1), .in_0(regfile_1_r1), .in_1(ex_mem_1_p10), .in_2(alu_1_out),
    .in_3({32{1'b0}}), .out(multiplexer_2_out));
  Multiplexer #(.Selector_Bits(2), .Bits(32)) multiplexer_3 (
    .sel(forwarding_unit_1_forward_cmp2), .in_0(regfile_1_r2), .in_1(ex_mem_1_p10), .in_2(alu_1_out),
    .in_3({32{1'b0}}), .out(multiplexer_3_out));
  Multiplexer #(.Bits(32)) multiplexer_4 (
    .sel(controller_1_r1_pc_sel), .in_0(multiplexer_2_out), .in_1(if_id_1_pc_out), .out(multiplexer_4_out));
  cmp cmp_1 (.op(controller_1_cmp_op), .in1(multiplexer_2_out), .in2(multiplexer_3_out), .out(cmp_1_out));
  Add #(.Bits(32)) add_1 (.a(multiplexer_4_out), .b(decode_1_imm), .c_i(1'b0), .s(add_1_s));  // open: c_o
  or or_2 (or_2_out, hazard_detection_unit_1_zero_idex, rst);
  // ID_EX id_ex_1: pin names not known; wires that end beside it: clk, or_2_out, if_id_1_pc_out, regfile_1_r1, regfile_1_r2, decode_1_rd, decode_1_imm, controller_1_memory_op, controller_1_alu_op, controller_1_r1_pc_sel, controller_1_r2_imm_sel, controller_1_rf_write, controller_1_rf_in_sel, decode_1_rs1, decode_1_rs2, id_ex_1_p16, id_ex_1_p17, id_ex_1_p18, id_ex_1_p19, id_ex_1_p20, id_ex_1_p21, id_ex_1_p22, id_ex_1_p23, id_ex_1_p24, id_ex_1_p25, id_ex_1_p26, id_ex_1_p27, id_ex_1_p28
  and and_1 (and_1_out, controller_1_pc_in_sel, cmp_1_out);
  forwarding_unit forwarding_unit_1 (
    .rs1_ID(decode_1_rs1), .rs2_ID(decode_1_rs2), .rs1_IDEX(id_ex_1_p27), .rs2_IDEX(id_ex_1_p28),
    .rd_IDEX(id_ex_1_p19), .write_IDEX(id_ex_1_p25), .rd_EXMEM(ex_mem_1_p13), .write_EXMEM(ex_mem_1_p14),
    .rd_MEMWB(mem_wb_1_rd_out), .write_MEMWB(mem_wb_1_rf_write_out),
    .forward_alu1(forwarding_unit_1_forward_alu1), .forward_alu2(forwarding_unit_1_forward_alu2),
    .forward_cmp1(forwarding_unit_1_forward_cmp1), .forward_cmp2(forwarding_unit_1_forward_cmp2));
  Multiplexer #(.Bits(32)) multiplexer_5 (
    .sel(id_ex_1_p23), .in_0(id_ex_1_p17), .in_1(id_ex_1_p16), .out(multiplexer_5_out));
  Multiplexer #(.Bits(32)) multiplexer_6 (
    .sel(id_ex_1_p24), .in_0(id_ex_1_p18), .in_1(id_ex_1_p20), .out(multiplexer_6_out));
  Multiplexer #(.Selector_Bits(2), .Bits(32)) multiplexer_7 (
    .sel(forwarding_unit_1_forward_alu1), .in_0(multiplexer_5_out), .in_1(multiplexer_9_out),
    .in_2(ex_mem_1_p10), .in_3({32{1'b0}}), .out(multiplexer_7_out));
  Multiplexer #(.Selector_Bits(2), .Bits(32)) multiplexer_8 (
    .sel(forwarding_unit_1_forward_alu2), .in_0(multiplexer_6_out), .in_1(multiplexer_9_out),
    .in_2(ex_mem_1_p10), .in_3({32{1'b0}}), .out(multiplexer_8_out));
  alu alu_1 (.op(id_ex_1_p22), .in1(multiplexer_7_out), .in2(multiplexer_8_out), .out(alu_1_out));
  // EX_MEM ex_mem_1: pin names not known; wires that end beside it: clk, rst, alu_1_out, id_ex_1_p21, multiplexer_8_out, id_ex_1_p19, id_ex_1_p25, id_ex_1_p26, id_ex_1_p16, ex_mem_1_p10, ex_mem_1_p11, ex_mem_1_p12, ex_mem_1_p13, ex_mem_1_p14, ex_mem_1_p15, ex_mem_1_p16
  not not_1 (not_1_out, ex_mem_1_p12[2]);
  and and_2 (and_2_out, not_1_out, ex_mem_1_p12[3]);
  memory memory_1 (
    .clk(clk), .rst(rst), .address(ex_mem_1_p10), .din(ex_mem_1_p11), .op(ex_mem_1_p12), .dout(memory_1_dout));
  Terminal terminal_1 (.D(ex_mem_1_p11), .C(clk), .en(and_2_out));
  MEM_WB mem_wb_1 (
    .clk(clk), .rst(rst), .rd(ex_mem_1_p13), .rf_write(ex_mem_1_p14), .rf_in_sel(ex_mem_1_p15),
    .alu_result(ex_mem_1_p10), .dout(memory_1_dout), .pc(ex_mem_1_p16), .rd_out(mem_wb_1_rd_out),
    .rf_write_out(mem_wb_1_rf_write_out), .rf_in_sel_out(mem_wb_1_rf_in_sel_out),
    .alu_result_out(mem_wb_1_alu_result_out), .dout_out(mem_wb_1_dout_out), .pc_out(mem_wb_1_pc_out));
  Add #(.Bits(32)) add_2 (.a(mem_wb_1_pc_out), .b(32'h4), .c_i(1'b0), .s(add_2_s));  // open: c_o
  Multiplexer #(.Selector_Bits(2), .Bits(32)) multiplexer_9 (
    .sel(mem_wb_1_rf_in_sel_out), .in_0(mem_wb_1_alu_result_out), .in_1(mem_wb_1_dout_out), .in_2(add_2_s),
    .in_3({32{1'b0}}), .out(multiplexer_9_out));

  // Notes on the sheet:
  //   clk: Hz: 10
endmodule
