// Digital circuit memory.dig as structural Verilog
// 数据存储器
module memory (
  input  clk,
  input  rst,
  input  [3:0] op,
  input  [31:0] din,
  input  [31:0] address,
  output [31:0] dout
);

  memory #(.applicationType("IVERILOG")) u_memory (
    .clk(clk), .rst(rst), .din(din), .op(op), .address(address), .dout(dout));

  // Notes on the sheet:
  //   op: 操作码
  //   din: 输入
  //   dout: 输出
endmodule

/* Code of memory:
// op = inst[5|14:12] = opcode[5] + funct[2:0]
`define LB 4'b0000
`define LH 4'b0001
`define LW 4'b0010
`define LBU 4'b0100
`define LHU 4'b0101
`define SB 4'b1000
`define SH 4'b1001
`define SW 4'b1010
`define DO_NOTHING 4'b1111

module memory(clk, rst, op, address, din, dout);
	input clk, rst;
	input [31:0] din;
	input [3:0] op;
	// 一切计算操作都放入ALU中，不再在memory中进行address=base+offset的计算
	// input [31:0] base;
	// input [31:0] offset;
	input [31:0] address;
	output [31:0] dout;
	
	reg [31:0] dout;
	// 存储空间 2^32 字节，以1字节=8位为一个单位，字节寻址
	// reg [7:0] memory[0:4294967295];
	// 2^32位太大，运行有问题，改为2^16字节
	reg [7:0] memory[0:65535];
		

	// 用于存储未经符号扩展的16位中间变量
	// reg [15:0] h_out;

	integer i;
	// integer address;

/*
	// 仅用于测试时初始化memory
	initial
	begin
		for (i = 0; i <= 65535; i++)
			begin
				memory[i] = i;
			end
	end
* /
	
	always @(op, address)
	begin
		case(op)
			`LB: 
			begin
				// 有符号扩展
				dout = $signed(memory[address]);
			end
			`LH:
			begin
				dout[15:8] = memory[address];
				dout[7:0] = memory[address+1];
				dout = $signed(dout);
			end
			`LW:
			begin
				dout[31:24] = memory[address];
				dout[23:16] = memory[address+1];
				dout[15:8] = memory[address+2];
				dout[7:0] = memory[address+3];
			end
			`LBU:
			begin
				// 无符号扩展
				dout = $unsigned(memory[address]);
			end
			`LHU:
			begin
				dout[15:8] = memory[address];
				dout[7:0] = memory[address+1];
				// dout = $unsigned(h_out);
			end
		endcase
	end
	
	always @(posedge clk)
	begin
		if (rst)
		begin
			for (i = 0; i <= 65535; i++)
			begin
				memory[i] = 0;
			end
		end
		else if (op == `DO_NOTHING)
		begin
			// 不做任何操作
		end
		else
		begin
			case(op)
				`SB:
				begin
					memory[address] = din[7:0];
					dout = din[7:0];
				end
				`SH:
				begin
					memory[address] = din[15:8];
					memory[address+1] = din[7:0];
					dout = din[15:0];
				end
				`SW:
				begin
					memory[address] = din[31:24];
					memory[address+1] = din[23:16];
					memory[address+2] = din[15:8];
					memory[address+3] = din[7:0];
					dout = din;
				end
			endcase
		end
	end

endmodule
*/
