// Digital circuit pc+4.dig as structural Verilog
module pc_4 (
  input  [31:0] pc,
  output [31:0] pc_out
);

  pc_add #(.applicationType("IVERILOG")) u_pc_add (.pc(pc), .pc_out(pc_out));
endmodule

/* Code of pc_add:
module pc_add(pc, pc_out);
	input [31:0] pc;
	output [31:0] pc_out;

	reg [31:0] pc_out;
	
	always @(pc)
	begin
		pc_out = pc+4;
	end
endmodule
*/
