// Digital circuit regfile.dig as structural Verilog
// 寄存器
module regfile (
  input  clk,
  input  [4:0] rs1,
  input  [4:0] rs2,
  input  [4:0] rd,
  input  write,
  input  [31:0] din,
  input  rst,
  output [31:0] r1,
  output [31:0] r2
);

  regfile #(.applicationType("IVERILOG")) u_regfile (
    .clk(clk), .rst(rst), .rs1(rs1), .rs2(rs2), .rd(rd), .write(write), .din(din), .r1(r1), .r2(r2));
endmodule

/* Code of regfile:
module regfile(clk, rst, rs1, rs2, rd, write, din, r1, r2);
	input clk, rst;
	input [4:0] rs1, rs2, rd;
	input write;
	input [31:0] din;
	output [31:0] r1, r2;

	reg [31:0] r[1:31];

	// 寄存器0号元素永远为0
	// assign r1 = (rs1 == 0)? 0: r[rs1];
	// assign r2 = (rs2 == 0)? 0: r[rs2];
	// 若要读的位置和当前要写的位置相同，则输出要写入的数，实现写先于读
	assign r1 = (rs1 == 0)? 0: (rs1 == rd && write == 1)? din: r[rs1];
	assign r2 = (rs2 == 0)? 0: (rs2 == rd && write == 1)? din: r[rs2];

	integer i;

/*
	// 下面代码仅用于测试
	initial
	begin
		// 为寄存器赋初始值
		for(i = 1; i < 32; i = i+1)
		begin
			r[i] = i;
		end
	end
* /

	always @(posedge clk)
	begin
		if (rst)
		begin
			// 如果rst=1，将栈清空
			for(i = 1; i < 32; i = i+1)
			begin
				r[i] = 0;
			end
		end
		// 如果write信号为1，则将din写入寄存器rd位置
		else if(write && rd != 0)
		begin
			r[rd] = din;
		end
	end

endmodule
*/
