// Digital circuit test.dig as structural Verilog
module test (
  input  [31:0] in,
  input  [31:0] in1,
  input  [7:0] in2,
  output [15:0] signed_out,
  output [15:0] unsigned_out,
  output [23:0] out1,
  output [7:0] out2
);

  test_32_16 #(.applicationType("IVERILOG")) u_test_32_16 (
    .in(in), .signed_out(signed_out), .unsigned_out(unsigned_out));
  test2 #(.applicationType("IVERILOG")) u_test2 (.in2(in2), .out2(out2));

  assign out1 = in1[23:0];
endmodule

/* Code of test_32_16:
module test_32_16(in, signed_out, unsigned_out);
	input [31:0] in;
	output [15:0] signed_out, unsigned_out;

	reg [15:0] signed_out, unsigned_out;	

	always @(in)
	begin
		signed_out = $signed(in);
		// unsigned_out = $unsigned(in);
		unsigned_out = in[15:0];
	end
endmodule
*/

/* Code of test2:
module test2(in2, out2);
	input [7:0] in2;
	output [7:0] out2;
	
	reg [7:0] out2;
	
	always @(in2)
	begin
		// out2 = $signed(in2[1:0]);
		// out2 = in2[1:0];
		out2[1:0] = in2[1:0];
		out2 = $signed(out2[1:0]);
	end
endmodule
*/
