// Digital circuit test_number.dig as structural Verilog
module test_number (
  input  [31:0] in,
  output [31:0] out
);

  BitExtender #(.outputBits(32)) bitextender_1 (.in(in[7:0]), .out(out));
endmodule
