// Digital circuit test_rom.dig as structural Verilog
module test_rom (
  input  [15:0] in,
  output [7:0] out
);

  ROM #(.AddrBits(16), .Bits(8)) code (.A(in), .sel(1'b1), .D(out));

  // Notes on the sheet:
  //   code loads instructs.hex
endmodule
